// Logisim project DragonArch.circ as structural Verilog: 6 circuits, main circuit main
module main (
  input  PCReset
);

  wire clock_1_out, clock_2_out, DataWrite, ImLoad, IRLoad, not_1_out, PCLoad, Write0, Write1, Write2;
  wire [1:0] AddrSelect, DataSelect, Op2Sel, PCSellect, RegSrc;
  wire [2:0] ir_1_registerselect0, ir_1_registerselect1, ir_1_registerselect2;
  wire [3:0] ALUCode, Opcode;
  wire [7:0] cu_1_ucounter;
  wire [15:0] ALUOut, gprs_1_registerout0, gprs_1_registerout1, gprs_1_registerout2, gprs_1_registerout3,
       gprs_1_registerout4, gprs_1_registerout5, gprs_1_registerout6, gprs_1_registerout7, Immed,
       multiplexer_1_out, multiplexer_2_out, multiplexer_3_out, multiplexer_4_out, PC, pc_1_pcout,
       ram_1_data, Read0, Read1, Read2, S_Register;

  // Probe on multiplexer_1_out
  Clock clock_1 (.out(clock_1_out));
  RAM #(.addrWidth(16), .dataWidth(16)) ram_1 (
    .addr(multiplexer_1_out), .data(ram_1_data), .clk(clock_1_out), .ld(not_1_out));  // open: sel, clr
  not not_1 (not_1_out, DataWrite);
  // Probe on cu_1_ucounter
  CU cu_1 (
    .ucounter(cu_1_ucounter), .opcode(Opcode), .aluop(ALUCode), .op2sel(Op2Sel), .datawrite(DataWrite),
    .addrsel(AddrSelect), .pcsel(PCSellect), .pcload(PCLoad), .dwrite(Write2), .irload(IRLoad),
    .imload(ImLoad), .regsrc(RegSrc), .datasel(DataSelect), .swrite(Write1));  // open: z, n, c
  Multiplexer #(.select(2), .width(16), .enable("false")) multiplexer_1 (
    .in0(pc_1_pcout), .in1(Immed), .in2(ALUOut), .in3(S_Register), .out(multiplexer_1_out), .sel(AddrSelect));
  // Probe on ram_1_data
  // Probe on pc_1_pcout
  assign ram_1_data = DataWrite ? multiplexer_2_out : 16'bz;  // Controlled_Buffer controlled_buffer_1
  Clock clock_2 (.out(clock_2_out));
  Multiplexer #(.select(2), .width(16), .enable("false")) multiplexer_2 (
    .in0(PC), .in1(Read0), .in2(Read1), .in3(ALUOut), .out(multiplexer_2_out), .sel(DataSelect));
  PC pc_1 (
    .ImmidiateRegister(Immed), .S_Register(S_Register), .PCOut(pc_1_pcout), .PCSelect(PCSellect),
    .PCLoad(PCLoad), .PCReset(PCReset));
  Register #(.width(16)) register_1 (.D(ram_1_data), .en(ImLoad), .Q(Immed), .clk(clock_2_out));  // open: clr
  IR ir_1 (
    .IRLoad(IRLoad), .instruction(ram_1_data), .Opcode(Opcode), .RegisterSelect0(ir_1_registerselect0),
    .RegisterSelect1(ir_1_registerselect1), .RegisterSelect2(ir_1_registerselect2));
  Multiplexer #(.select(2), .width(16), .enable("false")) multiplexer_3 (
    .in0(ram_1_data), .in1(Immed), .in2(ALUOut), .in3(S_Register), .out(multiplexer_3_out), .sel(RegSrc));
  GPRs gprs_1 (
    .Select0(ir_1_registerselect2), .RegisterIn(multiplexer_3_out), .RegisterOut0(gprs_1_registerout0),
    .RegisterOut1(gprs_1_registerout1), .RegisterOut2(gprs_1_registerout2),
    .RegisterOut3(gprs_1_registerout3), .RegisterOut4(gprs_1_registerout4),
    .RegisterOut5(gprs_1_registerout5), .RegisterOut6(gprs_1_registerout6),
    .RegisterOut7(gprs_1_registerout7), .Write0(Write0), .Write1(Write1), .Write2(Write2), .Read0(Read0),
    .Read1(Read2), .Read3(Read1), .Select1(ir_1_registerselect1), .Select2(ir_1_registerselect0));
  // Probe on gprs_1_registerout0
  // Probe on gprs_1_registerout1
  // Probe on gprs_1_registerout2
  // Probe on gprs_1_registerout3
  // Probe on gprs_1_registerout4
  // Probe on gprs_1_registerout5
  // Probe on gprs_1_registerout6
  // Probe on gprs_1_registerout7
  // Probe on ALUOut
  Multiplexer #(.select(2), .width(16), .enable("false")) multiplexer_4 (
    .in0(Read2), .in1(Immed), .in2({16{1'b0}}), .in3(16'h1), .out(multiplexer_4_out), .sel(Op2Sel));
  ALU alu_1 (.X(Read1), .Y(multiplexer_4_out), .Out(ALUOut), .ALU_code(ALUCode));

  // Notes on the sheet:
  //   Immediate Register
  //   Dragon Architecture 16-bit CPU
endmodule

module ALU (
  input  [3:0] ALU_code,
  input  [15:0] X,
  input  [15:0] Y,
  output [15:0] Out
);

  wire adder_1_cout, adder_2_cout, multiplexer_2_out, subtractor_1_bout, subtractor_2_bout, undriven;
  wire [1:0] undriven_2;
  wire [15:0] adder_1_out, adder_2_out, and_1_out, negator_1_out, or_1_out, subtractor_1_out,
       subtractor_2_out, xor_1_out;

  Adder #(.width(16)) adder_1 (.a(X), .b(X), .out(adder_1_out), .cin(undriven), .cout(adder_1_cout));
  Subtractor #(.width(16)) subtractor_1 (
    .a(X), .b(X), .out(subtractor_1_out), .bin(undriven), .bout(subtractor_1_bout));
  assign and_1_out = X & X;  // AND_Gate and_1, 16 bits wide
  assign or_1_out = X | X;  // OR_Gate or_1, 16 bits wide
  assign xor_1_out = X ^ X;  // XOR_Gate xor_1, 16 bits wide
  Negator #(.width(16)) negator_1 (.in(X), .out(negator_1_out));
  Adder #(.width(16)) adder_2 (.a(X), .b(16'h1), .out(adder_2_out), .cin(undriven), .cout(adder_2_cout));
  Subtractor #(.width(16)) subtractor_2 (
    .a(X), .b(16'h1), .out(subtractor_2_out), .bin(undriven), .bout(subtractor_2_bout));
  Multiplexer #(.select(4), .width(16), .enable("false")) multiplexer_1 (
    .in0(adder_1_out), .in1(subtractor_1_out), .in2(and_1_out), .in3(or_1_out), .in4(xor_1_out),
    .in5(negator_1_out), .in6(X), .in7(adder_2_out), .in8(subtractor_2_out), .out(Out), .sel(ALU_code));  // open: in9, in10, in11, in12, in13, in14, in15
  Multiplexer #(.select(2), .enable("false")) multiplexer_2 (
    .in0(adder_1_cout), .in1(subtractor_1_bout), .in2(adder_2_cout), .in3(subtractor_2_bout),
    .out(multiplexer_2_out), .sel(undriven_2));

  assign Y = X;

  // Notes on the sheet:
  //   CarryIn???
  //   Arithmetic Logic Unit
  //   ???
  //   ???
  //   CarryOut???
endmodule

module GPRs (
  input  Write0,
  input  Write1,
  input  Write2,
  input  [2:0] Select2,
  input  [2:0] Select1,
  input  [2:0] Select0,
  input  [15:0] RegisterIn,
  output [15:0] Read0,
  output [15:0] Read1,
  output [15:0] Read3,
  output [15:0] RegisterOut0,
  output [15:0] RegisterOut1,
  output [15:0] RegisterOut2,
  output [15:0] RegisterOut3,
  output [15:0] RegisterOut4,
  output [15:0] RegisterOut5,
  output [15:0] RegisterOut6,
  output [15:0] RegisterOut7
);

  wire Clock_out, demultiplexer_1_out0, demultiplexer_1_out1, demultiplexer_1_out2, demultiplexer_1_out3,
       demultiplexer_1_out4, demultiplexer_1_out5, demultiplexer_1_out6, demultiplexer_1_out7;

  Demultiplexer #(.select(3), .enable("false")) demultiplexer_1 (
    .out0(demultiplexer_1_out0), .out1(demultiplexer_1_out1), .out2(demultiplexer_1_out2),
    .out3(demultiplexer_1_out3), .out4(demultiplexer_1_out4), .out5(demultiplexer_1_out5),
    .out6(demultiplexer_1_out6), .out7(demultiplexer_1_out7), .in(Write0), .sel(Select0));
  Demultiplexer #(.select(3), .enable("false")) demultiplexer_2 (
    .out0(demultiplexer_1_out0), .out1(demultiplexer_1_out1), .out2(demultiplexer_1_out2),
    .out3(demultiplexer_1_out3), .out4(demultiplexer_1_out4), .out5(demultiplexer_1_out5),
    .out6(demultiplexer_1_out6), .out7(demultiplexer_1_out7), .in(Write1), .sel(Select1));
  Demultiplexer #(.select(3), .enable("false")) demultiplexer_3 (
    .out0(demultiplexer_1_out0), .out1(demultiplexer_1_out1), .out2(demultiplexer_1_out2),
    .out3(demultiplexer_1_out3), .out4(demultiplexer_1_out4), .out5(demultiplexer_1_out5),
    .out6(demultiplexer_1_out6), .out7(demultiplexer_1_out7), .in(Write2), .sel(Select2));
  Register #(.width(16)) Reg0 (
    .D(RegisterIn), .en(demultiplexer_1_out0), .Q(RegisterOut0), .clk(Clock_out));  // open: clr
  Register #(.width(16)) Reg1 (
    .D(RegisterIn), .en(demultiplexer_1_out1), .Q(RegisterOut1), .clk(Clock_out));  // open: clr
  Register #(.width(16)) Reg2 (
    .D(RegisterIn), .en(demultiplexer_1_out2), .Q(RegisterOut2), .clk(Clock_out));  // open: clr
  Register #(.width(16)) Reg3 (
    .D(RegisterIn), .en(demultiplexer_1_out3), .Q(RegisterOut3), .clk(Clock_out));  // open: clr
  Register #(.width(16)) Reg4 (
    .D(RegisterIn), .en(demultiplexer_1_out4), .Q(RegisterOut4), .clk(Clock_out));  // open: clr
  Register #(.width(16)) Reg5 (
    .D(RegisterIn), .en(demultiplexer_1_out5), .Q(RegisterOut5), .clk(Clock_out));  // open: clr
  Register #(.width(16)) Reg6 (
    .D(RegisterIn), .en(demultiplexer_1_out6), .Q(RegisterOut6), .clk(Clock_out));  // open: clr
  Register #(.width(16)) Reg7 (
    .D(RegisterIn), .en(demultiplexer_1_out7), .Q(RegisterOut7), .clk(Clock_out));  // open: clr
  Clock Clock (.out(Clock_out));
  Multiplexer #(.select(3), .width(16), .enable("false")) multiplexer_1 (
    .in0(RegisterOut0), .in1(RegisterOut1), .in2(RegisterOut2), .in3(RegisterOut3), .in4(RegisterOut4),
    .in5(RegisterOut5), .in6(RegisterOut6), .in7(RegisterOut7), .out(Read0), .sel(Select0));
  Multiplexer #(.select(3), .width(16), .enable("false")) multiplexer_2 (
    .in0(RegisterOut0), .in1(RegisterOut1), .in2(RegisterOut2), .in3(RegisterOut3), .in4(RegisterOut4),
    .in5(RegisterOut5), .in6(RegisterOut6), .in7(RegisterOut7), .out(Read1), .sel(Select1));
  Multiplexer #(.select(3), .width(16), .enable("false")) multiplexer_3 (
    .in0(RegisterOut0), .in1(RegisterOut1), .in2(RegisterOut2), .in3(RegisterOut3), .in4(RegisterOut4),
    .in5(RegisterOut5), .in6(RegisterOut6), .in7(RegisterOut7), .out(Read3), .sel(Select2));

  // Notes on the sheet:
  //   General Purpose Registers
endmodule

module IR (
  input  IRLoad,
  input  [15:0] instruction,
  output [3:0] Opcode,
  output [2:0] RegisterSelect0,
  output [2:0] RegisterSelect1,
  output [2:0] RegisterSelect2
);

  wire clock_1_out;
  wire [15:13] IR_q;

  Clock clock_1 (.out(clock_1_out));
  Register #(.width(16)) IR (
    .D(instruction), .en(IRLoad), .Q({IR_q, Opcode, RegisterSelect2, RegisterSelect1, RegisterSelect0}),
    .clk(clock_1_out));  // open: clr

  // Notes on the sheet:
  //   Instruction Register
endmodule

module PC (
  input  [15:0] ImmidiateRegister,
  input  PCLoad,
  input  PCReset,
  input  [15:0] S_Register,
  input  [1:0] PCSelect,
  output [15:0] PCOut
);

  wire clock_1_out;
  wire [15:0] adder_1_out, adder_2_out, multiplexer_1_out;

  Adder #(.width(16)) adder_1 (.a(PCOut), .b(16'h1), .out(adder_1_out));  // open: cin, cout
  Adder #(.width(16)) adder_2 (.a(PCOut), .b(ImmidiateRegister), .out(adder_2_out));  // open: cin, cout
  Multiplexer #(.select(2), .width(16), .enable("false")) multiplexer_1 (
    .in0(adder_1_out), .in1(ImmidiateRegister), .in2(adder_2_out), .in3(S_Register), .out(multiplexer_1_out),
    .sel(PCSelect));
  Clock clock_1 (.out(clock_1_out));
  Register #(.width(16)) PCReg (.D(multiplexer_1_out), .en(PCLoad), .Q(PCOut), .clk(clock_1_out), .clr(PCReset));

  // Notes on the sheet:
  //   Program Counter
endmodule

module CU (
  input  z,
  input  n,
  input  c,
  input  [3:0] opcode,
  output [3:0] aluop,
  output [1:0] op2sel,
  output datawrite,
  output [7:0] ucounter,
  output [1:0] addrsel,
  output [1:0] pcsel,
  output pcload,
  output dwrite,
  output irload,
  output imload,
  output [1:0] regsrc,
  output [1:0] datasel,
  output swrite
);

  wire clock_1_out, indexsel, multiplexer_2_out, or_1_out;
  wire [1:0] cond;
  wire [7:0] adder_1_out, multiplexer_1_out, multiplexer_3_out;
  wire [15:0] rom_2_data;
  wire [31:23] rom_1_data;

  Register Microcounter (.D(adder_1_out), .Q(ucounter), .clk(clock_1_out));  // open: en, clr
  Clock clock_1 (.out(clock_1_out));
  ROM #(.dataWidth(32)) rom_1 (
    .addr(ucounter),
    .data({rom_1_data, swrite, datasel, indexsel, cond, regsrc, imload, irload, dwrite, pcload, pcsel, addrsel, datawrite, op2sel, aluop}));  // open: sel
  ROM #(.dataWidth(16)) rom_2 (.addr(ucounter), .data(rom_2_data));  // open: sel
  or or_1 (or_1_out, z, n);
  Multiplexer #(.width(8), .enable("false")) multiplexer_1 (
    .in0(rom_2_data[7:0]), .in1(rom_2_data[15:8]), .out(multiplexer_1_out), .sel(multiplexer_2_out));
  Multiplexer #(.select(2), .enable("false")) multiplexer_2 (
    .in0(z), .in1(or_1_out), .in2(n), .in3(c), .out(multiplexer_2_out), .sel(cond));
  Multiplexer #(.width(8), .enable("false")) multiplexer_3 (
    .in0({8{1'b0}}), .in1({4'b0000, opcode}), .out(multiplexer_3_out), .sel(indexsel));
  Adder adder_1 (.a(multiplexer_1_out), .b(multiplexer_3_out), .out(adder_1_out));  // open: cin, cout

  // Notes on the sheet:
  //   Control ROM
  //   Decision ROM
endmodule
